// Logisim project MStty-2 - OTRO.circ as structural Verilog: 3 circuits, main circuit main
module main (
);

  wire a_t, alu_1_z, b, clk, FZ, fz_t, ir, nL_E, not_1_out, pc_t, reset, tty_out_1_clr, tty_out_1_out;
  wire [1:0] alu, CO, mux;
  wire [2:0] estado, rom_1_data;
  wire [6:0] A, adder_1_out, D, D6_0, F, PC;
  wire [15:0] A_q, B_q, ram_1_data;
  wire [15:7] alu_1_s;

  Register #(.width(3)) u_estado (.D(rom_1_data), .Q(estado), .clk(clk), .clr(reset));  // open: en
  Register #(.width(7)) u_PC (.D(adder_1_out), .en(pc_t), .Q(PC), .clk(clk), .clr(reset));
  Register #(.width(16)) u_IR (.D(ram_1_data), .en(ir), .Q({CO, F, D}), .clk(clk));  // open: clr
  Multiplexer #(.select(2), .width(7), .enable("false")) multiplexer_1 (
    .in0(PC), .in2(F), .in3(D), .out(A), .sel(mux));  // open: in1
  ROM #(.addrWidth(3), .dataWidth(3)) rom_1 (.addr({CO, FZ}), .data(rom_1_data));  // open: sel
  ROM #(.addrWidth(3), .dataWidth(10)) rom_2 (
    .addr(estado), .data({mux, alu, nL_E, pc_t, ir, a_t, b, fz_t}));  // open: sel
  Adder #(.width(7)) adder_1 (.a(7'b0000001), .b(A), .out(adder_1_out));  // open: cin, cout
  Register #(.width(16)) u_A (.D(ram_1_data), .en(a_t), .Q(A_q), .clk(clk));  // open: clr
  Register #(.width(1)) u_FZ (.D(alu_1_z), .en(fz_t), .Q(FZ), .clk(clk));  // open: clr
  ALU alu_1 (.A(A_q), .B(B_q), .T(alu), .Z(alu_1_z), .S({alu_1_s, D6_0}));
  // Probe on PC
  // Probe on CO
  Register #(.width(16)) u_B (.D(ram_1_data), .en(b), .Q(B_q), .clk(clk));  // open: clr
  Button button_1 (.out(reset));
  Clock clock_1 (.out(clk));
  // Probe on F
  // Probe on D
  RAM #(.addrWidth(7), .dataWidth(16), .bus("separate")) ram_1 (
    .addr(A), .din({alu_1_s, D6_0}), .data(ram_1_data), .str(nL_E), .sel(1'b1), .clk(clk), .ld(not_1_out));  // open: clr
  not not_1 (not_1_out, nL_E);
  // Probe on estado
  TTY tty_1 (.data(D6_0), .clk(clk), .we(tty_out_1_out), .clr(tty_out_1_clr));
  tty_out tty_out_1 (.A(A), .E(nL_E), .out(tty_out_1_out), .clr(tty_out_1_clr), .D(D6_0), .clk(clk));
  Counter CICN ();  // open: load, D, count, Q, carry, clk, clr
  Counter INSN ();  // open: load, D, count, Q, carry, clk, clr

  // Notes on the sheet:
  //   Unidad de Control (cableada 12 estados)
  //   Unidad de Proceso (ruta de datos)
  //   contents of rom_1 (hex, n*v repeats v):
  //   8*1
  //   contents of rom_2 (hex, n*v repeats v):
  //   18 0 202 202 202 0 304 321
  //   Control de simulación
  //   0 ADD
  //   1 CMP
  //   2 MOV
  //   3 BEQ
endmodule

module ALU (
  input  [15:0] A,
  input  [15:0] B,
  input  [1:0] T,
  output Z,
  output [15:0] S
);

  wire [15:0] adder_1_out, xor_1_out;

  Adder #(.width(16)) adder_1 (.a(A), .b(B), .out(adder_1_out));  // open: cin, cout
  Multiplexer #(.select(2), .width(16), .enable("false")) multiplexer_1 (
    .in0(adder_1_out), .in1(xor_1_out), .in2(B), .out(S), .sel(T));  // open: in3
  assign xor_1_out = A ^ B;  // XOR_Gate xor_1, 16 bits wide
  nor nor_1 (Z, S[0], S[1], S[2], S[3], S[4], S[5], S[6], S[7], S[8], S[9], S[10], S[11], S[12], S[13], S[14], S[15]);
endmodule

module tty_out (
  input  clk,
  input  [6:0] A,
  input  E,
  input  [6:0] D,
  output out,
  output clr
);

  wire and_2_out, and_3_out;

  and and_1 (out, A[0], A[1], A[2], A[3], A[4], A[5], A[6], E);
  and and_2 (and_2_out, ~D[0], ~D[1], ~D[2], ~D[3], ~D[4], ~D[5], ~D[6]);  // AND_Gate
  and and_3 (and_3_out, out, and_2_out);
  D_Flip_Flop d_ff_1 (.clk(clk), .D(and_3_out), .Q(clr), .en(1'b1));  // open: Qn, preset, reset
endmodule
