// Logisim project Practica 5h.circ as structural Verilog: 11 circuits, main circuit FA
module FA (
  input  A,
  input  B,
  input  Cin,
  output S,
  output Cout
);

  wire and_1_out, and_2_out, xor_1_out;

  xor xor_1 (xor_1_out, A, B);
  and and_1 (and_1_out, Cin, xor_1_out);
  and and_2 (and_2_out, A, B);
  xor xor_2 (S, xor_1_out, Cin);
  or or_1 (Cout, and_1_out, and_2_out);
endmodule

module RCA16 (
  input  Cin,
  input  [15:0] A,
  input  [15:0] B,
  output Cout,
  output [15:0] S
);

  wire fa_1_cout, fa_2_cout, fa_3_cout, fa_4_cout, fa_5_cout, fa_6_cout, fa_7_cout, fa_8_cout, fa_9_cout,
       fa_10_cout, fa_11_cout, fa_12_cout, fa_13_cout, fa_14_cout, fa_15_cout;

  // Probe on A
  // Probe on B
  // Probe on S
  FA fa_1 (.A(A[0]), .B(B[0]), .Cin(Cin), .S(S[0]), .Cout(fa_1_cout));
  FA fa_2 (.A(A[1]), .B(B[1]), .Cin(fa_1_cout), .S(S[1]), .Cout(fa_2_cout));
  FA fa_3 (.A(A[2]), .B(B[2]), .Cin(fa_2_cout), .S(S[2]), .Cout(fa_3_cout));
  FA fa_4 (.A(A[3]), .B(B[3]), .Cin(fa_3_cout), .S(S[3]), .Cout(fa_4_cout));
  FA fa_5 (.A(A[4]), .B(B[4]), .Cin(fa_4_cout), .S(S[4]), .Cout(fa_5_cout));
  FA fa_6 (.A(A[5]), .B(B[5]), .Cin(fa_5_cout), .S(S[5]), .Cout(fa_6_cout));
  FA fa_7 (.A(A[6]), .B(B[6]), .Cin(fa_6_cout), .S(S[6]), .Cout(fa_7_cout));
  FA fa_8 (.A(A[7]), .B(B[7]), .Cin(fa_7_cout), .S(S[7]), .Cout(fa_8_cout));
  FA fa_9 (.A(A[8]), .B(B[8]), .Cin(fa_8_cout), .S(S[8]), .Cout(fa_9_cout));
  FA fa_10 (.A(A[9]), .B(B[9]), .Cin(fa_9_cout), .S(S[9]), .Cout(fa_10_cout));
  FA fa_11 (.A(A[10]), .B(B[10]), .Cin(fa_10_cout), .S(S[10]), .Cout(fa_11_cout));
  FA fa_12 (.A(A[11]), .B(B[11]), .Cin(fa_11_cout), .S(S[11]), .Cout(fa_12_cout));
  FA fa_13 (.A(A[12]), .B(B[12]), .Cin(fa_12_cout), .S(S[12]), .Cout(fa_13_cout));
  FA fa_14 (.A(A[13]), .B(B[13]), .Cin(fa_13_cout), .S(S[13]), .Cout(fa_14_cout));
  FA fa_15 (.A(A[14]), .B(B[14]), .Cin(fa_14_cout), .S(S[14]), .Cout(fa_15_cout));
  FA fa_16 (.A(A[15]), .B(B[15]), .Cin(fa_15_cout), .S(S[15]), .Cout(Cout));
endmodule

module XOR16 (
  input  [15:0] A,
  input  [15:0] B,
  output [15:0] S
);

  // Probe on A
  // Probe on B
  // Probe on S
  xor xor_1 (S[0], A[0], B[0]);
  xor xor_2 (S[1], A[1], B[1]);
  xor xor_3 (S[2], A[2], B[2]);
  xor xor_4 (S[3], A[3], B[3]);
  xor xor_5 (S[4], A[4], B[4]);
  xor xor_6 (S[5], A[5], B[5]);
  xor xor_7 (S[6], A[6], B[6]);
  xor xor_8 (S[7], A[7], B[7]);
  xor xor_9 (S[8], A[8], B[8]);
  xor xor_10 (S[9], A[9], B[9]);
  xor xor_11 (S[10], A[10], B[10]);
  xor xor_12 (S[11], A[11], B[11]);
  xor xor_13 (S[12], A[12], B[12]);
  xor xor_14 (S[13], A[13], B[13]);
  xor xor_15 (S[14], A[14], B[14]);
  xor xor_16 (S[15], A[15], B[15]);
endmodule

module MUX4_1 (
  input  S0,
  input  S1,
  input  X3,
  input  X2,
  input  X1,
  input  X0,
  output z
);

  wire and_1_out, and_2_out, and_3_out, and_4_out, not_1_out, not_2_out;

  not not_1 (not_1_out, S0);
  not not_2 (not_2_out, S1);
  and and_1 (and_1_out, S0, X0, S1);
  and and_2 (and_2_out, S0, X1, not_2_out);
  and and_3 (and_3_out, not_1_out, X2, S1);
  and and_4 (and_4_out, not_2_out, X3, not_1_out);
  or or_1 (z, and_1_out, and_2_out, and_3_out, and_4_out);

  // Notes on the sheet:
  //   dx0 --> z=20+20=40ps
  //   dx1 --> z=20+20=40ps
  //   dx2 --> z=20+20=40ps
  //   dx3 --> z=20+20=40ps
  //   ds1 --> z=5+20+20=45ps
  //   ds0 --> z=5+20+20=45ps
endmodule

module MUX_4_1x16 (
  input  T0,
  input  T1,
  input  [15:0] X0,
  input  [15:0] X1,
  input  [15:0] X2,
  input  [15:0] X3,
  output [15:0] S
);

  MUX4_1 mux4_1_1 (.X3(X0[0]), .X2(X1[0]), .X1(X2[0]), .X0(X3[0]), .S0(T0), .S1(T1), .z(S[0]));
  MUX4_1 mux4_1_2 (.X3(X0[1]), .X2(X1[1]), .X1(X2[1]), .X0(X3[1]), .S0(T0), .S1(T1), .z(S[1]));
  MUX4_1 mux4_1_3 (.X3(X0[2]), .X2(X1[2]), .X1(X2[2]), .X0(X3[2]), .S0(T0), .S1(T1), .z(S[2]));
  MUX4_1 mux4_1_4 (.X3(X0[3]), .X2(X1[3]), .X1(X2[3]), .X0(X3[3]), .S0(T0), .S1(T1), .z(S[3]));
  MUX4_1 mux4_1_5 (.X3(X0[4]), .X2(X1[4]), .X1(X2[4]), .X0(X3[4]), .S0(T0), .S1(T1), .z(S[4]));
  MUX4_1 mux4_1_6 (.X3(X0[5]), .X2(X1[5]), .X1(X2[5]), .X0(X3[5]), .S0(T0), .S1(T1), .z(S[5]));
  MUX4_1 mux4_1_7 (.X3(X0[6]), .X2(X1[6]), .X1(X2[6]), .X0(X3[6]), .S0(T0), .S1(T1), .z(S[6]));
  MUX4_1 mux4_1_8 (.X3(X0[7]), .X2(X1[7]), .X1(X2[7]), .X0(X3[7]), .S0(T0), .S1(T1), .z(S[7]));
  // Probe on X0
  // Probe on X1
  MUX4_1 mux4_1_9 (.X3(X0[8]), .X2(X1[8]), .X1(X2[8]), .X0(X3[8]), .S0(T0), .S1(T1), .z(S[8]));
  MUX4_1 mux4_1_10 (.X3(X0[9]), .X2(X1[9]), .X1(X2[9]), .X0(X3[9]), .S0(T0), .S1(T1), .z(S[9]));
  MUX4_1 mux4_1_11 (.X3(X0[10]), .X2(X1[10]), .X1(X2[10]), .X0(X3[10]), .S0(T0), .S1(T1), .z(S[10]));
  MUX4_1 mux4_1_12 (.X3(X0[11]), .X2(X1[11]), .X1(X2[11]), .X0(X3[11]), .S0(T0), .S1(T1), .z(S[11]));
  MUX4_1 mux4_1_13 (.X3(X0[12]), .X2(X1[12]), .X1(X2[12]), .X0(X3[12]), .S0(T0), .S1(T1), .z(S[12]));
  MUX4_1 mux4_1_14 (.X3(X0[13]), .X2(X1[13]), .X1(X2[13]), .X0(X3[13]), .S0(T0), .S1(T1), .z(S[13]));
  MUX4_1 mux4_1_15 (.X3(X0[14]), .X2(X1[14]), .X1(X2[14]), .X0(X3[14]), .S0(T0), .S1(T1), .z(S[14]));
  MUX4_1 mux4_1_16 (.X3(X0[15]), .X2(X1[15]), .X1(X2[15]), .X0(X3[15]), .S0(T0), .S1(T1), .z(S[15]));
  // Probe on X2
  // Probe on X3
  // Probe on S
endmodule

module ALU (
  input  [15:0] A,
  input  [15:0] B,
  input  T1,
  input  T0,
  output [15:0] out_5,
  output [3:0] NZVC
);

  wire Cout0, Cout1;
  wire [15:0] not_1_out, rca16_1_s, rca16_2_s, xor16_1_s;

  // Probe on A
  // Probe on B
  // Probe on out_5
  RCA16 rca16_1 (.A(A), .B(B), .Cin(1'b0), .Cout(Cout0), .S(rca16_1_s));
  XOR16 xor16_1 (.A(A), .B(B), .S(xor16_1_s));
  assign not_1_out = ~A;  // NOT_Gate not_1, 16 bits wide
  RCA16 rca16_2 (.A(not_1_out), .B(B), .Cin(1'b1), .Cout(Cout1), .S(rca16_2_s));
  MUX_4_1x16 mux_4_1x16_1 (.X0(rca16_1_s), .X1(B), .X2(xor16_1_s), .X3(rca16_2_s), .T0(T0), .T1(T1), .S(out_5));
  FLAGS flags_1 (
    .S(out_5), .A(A), .B(B), .T0(T0), .T1(T1), .Cout0(Cout0), .Cout1(Cout1), .N(NZVC[3]), .Z(NZVC[2]),
    .V(NZVC[1]), .C(NZVC[0]));

  // Other names for the same wires on the sheet: S[15:0] = out_5

  // Notes on the sheet:
  //   dmax B --> z=XOR+SUMADOR+MUX+NOR
  //   dmax B --> z=30+(30+20+20+(20+20)*14+30)+40+55=  785 ps
  //   Es decir: 1.27 Goperaciones/segundo
  //   Por lo tanto, F = 1/s = 1/(785*10^ -12) = 1273885350 operaciones/segundo
endmodule

module FLAGS (
  input  [15:0] S,
  input  [15:0] A,
  input  [15:0] B,
  input  T0,
  input  T1,
  input  Cout0,
  input  Cout1,
  output N,
  output Z,
  output V,
  output C
);

  wire and_1_out, and_2_out, and_3_out, and_4_out, or_2_out;

  or or_1 (C, Cout0, Cout1);
  nor nor_1 (Z, S[0], S[1], S[2], S[3], S[4], S[5], S[6], S[7], S[9], S[10], S[11], S[12], S[13], S[14], S[15], S[8]);
  and and_1 (and_1_out, T0, ~B[15]);  // AND_Gate
  and and_2 (and_2_out, B[15], ~T1);  // AND_Gate
  or or_2 (or_2_out, and_1_out, and_2_out);
  and and_3 (and_3_out, S[15], ~or_2_out, ~A[15]);  // AND_Gate
  and and_4 (and_4_out, A[15], or_2_out, ~S[15]);  // AND_Gate
  or or_3 (V, and_3_out, and_4_out);

  assign N = S[15];

  // Notes on the sheet:
  //   FLAGS
endmodule

module Add_Gen (
  input  reset_star,
  input  clk,
  input  en,
  output [2:0] Q2_0,
  output fin
);

  wire and_1_out, and_2_out, and_3_out, not_1_out, not_2_out, not_3_out, not_4_out, or_1_out, or_2_out,
       or_3_out, or_4_out;

  not not_1 (not_1_out, en);
  not not_2 (not_2_out, Q2_0[2]);
  not not_3 (not_3_out, Q2_0[1]);
  not not_4 (not_4_out, Q2_0[0]);
  and and_1 (and_1_out, en, Q2_0[0]);
  and and_2 (and_2_out, en, Q2_0[0]);
  or or_1 (or_1_out, en, Q2_0[2]);
  or or_2 (or_2_out, Q2_0[2], Q2_0[1]);
  or or_3 (or_3_out, Q2_0[2], Q2_0[0]);
  or or_4 (or_4_out, not_1_out, not_2_out, not_3_out, not_4_out);
  and and_3 (and_3_out, or_1_out, or_2_out, or_3_out, or_4_out);
  D_Flip_Flop d_ff_1 (.clk(clk), .D(and_3_out), .Q(Q2_0[2]), .reset(reset_star));  // open: Qn, preset, en
  J_K_Flip_Flop j_k_ff_1 (
    .J(and_1_out), .clk(clk), .K(and_2_out), .Q(Q2_0[1]), .reset(reset_star));  // open: Qn, preset, en
  T_Flip_Flop t_ff_1 (.clk(clk), .T(en), .Q(Q2_0[0]), .reset(reset_star));  // open: Qn, preset, en
  and and_4 (fin, Q2_0[0], Q2_0[1], Q2_0[2]);

  // Other names for the same wires on the sheet: q0 = Q2_0[0]; q1 = Q2_0[1]; q2 = Q2_0[2]

  // Notes on the sheet:
  //   dfin = 40+20 = 60
  //   dq1 = 20
  //   dq2 = 20+20= 40
  //   dq0 = 20
endmodule

module FD (
  input  [1:0] FLAG,
  input  [3:0] NZVC,
  output STOP
);

  wire and_1_out, and_2_out, and_3_out, and_4_out, not_1_out, not_2_out, not_3_out, not_4_out;

  not not_1 (not_1_out, FLAG[1]);
  not not_2 (not_2_out, FLAG[0]);
  not not_3 (not_3_out, FLAG[1]);
  not not_4 (not_4_out, FLAG[0]);
  and and_1 (and_1_out, not_1_out, not_2_out, NZVC[3]);
  and and_2 (and_2_out, not_3_out, FLAG[0], NZVC[2]);
  and and_3 (and_3_out, FLAG[1], not_4_out, NZVC[1]);
  and and_4 (and_4_out, FLAG[1], FLAG[0], NZVC[0]);
  or or_1 (STOP, and_1_out, and_2_out, and_3_out, and_4_out);
endmodule

module U_C (
  input  reset,
  input  clk,
  input  stop,
  input  \end ,
  output acc_en,
  output mdr_en,
  output ag_en
);

  wire q0, q1;
  wire [1:0] rom_1_data;

  ROM #(.addrWidth(4), .dataWidth(2)) rom_1 (.addr({\end , stop, q1, q0}), .data(rom_1_data));  // open: sel
  D_Flip_Flop d_ff_1 (.clk(clk), .D(rom_1_data[0]), .Q(q1), .reset(reset));  // open: Qn, preset, en
  D_Flip_Flop d_ff_2 (.clk(clk), .D(rom_1_data[1]), .Q(q0), .reset(reset));  // open: Qn, preset, en
  ROM #(.addrWidth(2), .dataWidth(3)) rom_2 (.addr(rom_1_data), .data({ag_en, mdr_en, acc_en}));  // open: sel

  // Notes on the sheet:
  //   contents of rom_1 (hex, n*v repeats v):
  //   0 2 6*3 1 2 6*3
  //   contents of rom_2 (hex, n*v repeats v):
  //   7 3 1
endmodule

module ACUMULADOR (
  input  [1:0] flag,
  input  reset_star
);

  wire acc_en, ag_en, CLK, END, fd_1_stop, mdr_en;
  wire [2:0] add_gen_1_q2_0;
  wire [3:0] NZVC;
  wire [15:0] MDR_q, minus_ACC, minus_ALU, rom_1_data;

  Clock u_clk (.out(CLK));
  Add_Gen add_gen_1 (.reset_star(reset_star), .clk(CLK), .en(ag_en), .Q2_0(add_gen_1_q2_0), .fin(END));
  FD fd_1 (.FLAG(flag), .NZVC(NZVC), .STOP(fd_1_stop));
  U_C u_c_1 (
    .reset(reset_star), .clk(CLK), .stop(fd_1_stop), .\end (END), .acc_en(acc_en), .mdr_en(mdr_en),
    .ag_en(ag_en));
  ROM #(.addrWidth(3), .dataWidth(16)) rom_1 (.addr(add_gen_1_q2_0), .data(rom_1_data));  // open: sel
  Register #(.width(16)) MDR (.D(rom_1_data), .en(mdr_en), .Q(MDR_q), .clk(CLK), .clr(reset_star));
  // Probe on minus_ALU
  Register #(.width(16)) ACC (.D(minus_ACC), .en(acc_en), .Q(minus_ALU), .clk(CLK), .clr(reset_star));
  ALU alu_1 (.A(minus_ALU), .B(MDR_q), .T1(1'b0), .T0(1'b0), .out_5(minus_ACC), .NZVC(NZVC));

  // Notes on the sheet:
  //   contents of rom_1 (hex, n*v repeats v):
  //   7*1 1111
endmodule
