// Logisim project Practica1.1.circ as structural Verilog: 1 circuit, main circuit main
module main (
  input  x1,
  input  w,
  input  x0,
  output z,
  output y
);

  wire transistor_5_out;

  Transistor transistor_1 (.in(1'b1), .out(z), .gate(w));
  Transistor #(.\type ("n")) transistor_2 (.in(1'b0), .out(z), .gate(w));
  Transistor transistor_3 (.in(1'b1), .out(y), .gate(x1));
  Transistor #(.\type ("n")) transistor_4 (.in(transistor_5_out), .out(y), .gate(x1));
  Transistor #(.\type ("n")) transistor_5 (.in(1'b0), .out(transistor_5_out), .gate(x0));
  Transistor transistor_6 (.in(1'b1), .out(y), .gate(x0));

  // Notes on the sheet:
  //   NOT
  //   NAND
endmodule
