// Logisim project Practica3.circ as structural Verilog: 3 circuits, main circuit main
module main (
  input  A3,
  input  A2,
  input  A1,
  input  A0,
  input  B3,
  input  B2,
  input  B1,
  input  B0
);

  wire a, a1_t, a2_t, b, b1_t, b2_t, c, c1, c2, d, d1, d2, e, e1, e2, f, f1, f2, g, g1, g2, s, S0, S1, S2,
       s2_t, S3, sy;

  Numeros_enteros numeros_enteros_1 (
    .x3(A3), .x2(A2), .x1(A1), .x0(A0), .s(s), .a(a), .b(b), .c(c), .d(d), .e(e), .f(f), .g(g));
  Numeros_enteros numeros_enteros_2 (
    .x3(B3), .x2(B2), .x1(B1), .x0(B0), .s(sy), .a(a1_t), .b(b1_t), .c(c1), .d(d1), .e(e1), .f(f1), .g(g1));
  RCA4 rca4_1 (
    .A0(A0), .B0(B0), .C0(1'b0), .A1(A1), .B1(B1), .A2(A2), .B2(B2), .A3(A3), .B3(B3), .S0(S0), .S1(S1),
    .S2(S2), .S3(S3));  // open: C4
  Numeros_enteros numeros_enteros_3 (
    .x3(S3), .x2(S2), .x1(S1), .x0(S0), .s(s2_t), .a(a2_t), .b(b2_t), .c(c2), .d(d2), .e(e2), .f(f2), .g(g2));
  _7_Segment_Display u_7_segment_display_1 (.g(g), .f(f), .a(a), .b(b), .e(e), .d(d), .c(c));  // open: dp
  _7_Segment_Display u_7_segment_display_2 (.g(s));  // open: f, a, b, e, d, c, dp
  _7_Segment_Display u_7_segment_display_3 (.g(sy));  // open: f, a, b, e, d, c, dp
  _7_Segment_Display u_7_segment_display_4 (.g(s2_t));  // open: f, a, b, e, d, c, dp
  _7_Segment_Display u_7_segment_display_5 (.g(g1), .f(f1), .a(a1_t), .b(b1_t), .e(e1), .d(d1), .c(c1));  // open: dp
  _7_Segment_Display u_7_segment_display_6 (.g(g2), .f(f2), .a(a2_t), .b(b2_t), .e(e2), .d(d2), .c(c2));  // open: dp

  // Notes on the sheet:
  //   Numero A
  //   Numero B
  //   Visualizador de enteros
  //   Visualizador de enteros
endmodule

module Numeros_enteros (
  input  x3,
  input  x2,
  input  x1,
  input  x0,
  output s,
  output a,
  output b,
  output c,
  output d,
  output e,
  output f,
  output g
);

  wire and_1_out, and_2_out, and_3_out, and_4_out, and_5_out, and_6_out, and_7_out, and_8_out, and_9_out,
       and_10_out, and_11_out, and_12_out, and_13_out, and_14_out, and_15_out, and_16_out, and_17_out,
       and_18_out, and_19_out, and_20_out, and_21_out, and_22_out, and_23_out, and_24_out, and_25_out,
       and_26_out, not_1_out, not_2_out, not_3_out, not_4_out, not_5_out, not_6_out, not_7_out, not_8_out,
       not_9_out, not_10_out, not_11_out, not_12_out, not_13_out, not_14_out, not_15_out, not_16_out,
       not_17_out, not_18_out, not_19_out, not_20_out, not_21_out, not_22_out, not_23_out, not_24_out,
       not_25_out, not_26_out, not_27_out, not_28_out, not_29_out, not_30_out, not_31_out, not_32_out,
       not_33_out, not_34_out, not_35_out;

  not not_1 (not_1_out, x2);
  and and_1 (and_1_out, not_1_out, not_2_out);
  not not_2 (not_2_out, x0);
  not not_3 (not_3_out, x3);
  and and_2 (and_2_out, not_3_out, x1);
  and and_3 (and_3_out, x1, not_4_out);
  not not_4 (not_4_out, x0);
  and and_4 (and_4_out, x2, not_5_out, x0);
  not not_5 (not_5_out, x1);
  and and_5 (and_5_out, x3, not_6_out);
  not not_6 (not_6_out, x2);
  not not_7 (not_7_out, x3);
  and and_6 (and_6_out, not_7_out, not_8_out);
  not not_8 (not_8_out, x2);
  not not_9 (not_9_out, x2);
  and and_7 (and_7_out, not_9_out, not_10_out);
  not not_10 (not_10_out, x1);
  not not_11 (not_11_out, x1);
  and and_8 (and_8_out, not_11_out, not_12_out);
  not not_12 (not_12_out, x0);
  not not_13 (not_13_out, x3);
  and and_9 (and_9_out, not_13_out, x1, x0);
  and and_10 (and_10_out, x3, x2);
  not not_14 (not_14_out, x1);
  not not_15 (not_15_out, x3);
  and and_11 (and_11_out, not_15_out, x2);
  and and_12 (and_12_out, x3, not_16_out);
  not not_16 (not_16_out, x2);
  not not_17 (not_17_out, x2);
  and and_13 (and_13_out, not_17_out, not_18_out);
  not not_18 (not_18_out, x0);
  not not_19 (not_19_out, x2);
  and and_14 (and_14_out, not_19_out, x1);
  and and_15 (and_15_out, x1, not_20_out);
  not not_20 (not_20_out, x0);
  and and_16 (and_16_out, x2, not_21_out, x0);
  not not_21 (not_21_out, x1);
  not not_22 (not_22_out, x2);
  and and_17 (and_17_out, not_22_out, not_23_out);
  not not_23 (not_23_out, x0);
  and and_18 (and_18_out, x1, not_24_out);
  not not_24 (not_24_out, x0);
  not not_25 (not_25_out, x1);
  and and_19 (and_19_out, not_25_out, not_26_out);
  not not_26 (not_26_out, x0);
  not not_27 (not_27_out, x3);
  and and_20 (and_20_out, not_27_out, x2, not_28_out);
  not not_28 (not_28_out, x1);
  not not_29 (not_29_out, x3);
  and and_21 (and_21_out, not_29_out, x2, not_30_out);
  not not_30 (not_30_out, x0);
  and and_22 (and_22_out, x3, not_31_out, x1);
  not not_31 (not_31_out, x2);
  not not_32 (not_32_out, x2);
  and and_23 (and_23_out, not_32_out, x1);
  and and_24 (and_24_out, x1, not_33_out);
  not not_33 (not_33_out, x0);
  and and_25 (and_25_out, x2, not_34_out);
  not not_34 (not_34_out, x1);
  and and_26 (and_26_out, x3, not_35_out);
  not not_35 (not_35_out, x0);
  or or_1 (a, and_1_out, and_2_out, and_3_out, and_4_out, and_5_out);
  or or_2 (b, and_6_out, and_7_out, and_8_out, and_9_out, and_10_out);
  or or_3 (c, not_14_out, x0, and_11_out, and_12_out);
  or or_4 (d, and_13_out, and_14_out, and_15_out, and_16_out);
  or or_5 (e, and_17_out, and_18_out);
  or or_6 (f, and_19_out, and_20_out, and_21_out, and_22_out);
  or or_7 (g, and_23_out, and_24_out, and_25_out, and_26_out);

  assign s = x3;
endmodule

module RCA4 (
  input  A0,
  input  B0,
  input  C0,
  input  A1,
  input  B1,
  input  A2,
  input  B2,
  input  A3,
  input  B3,
  output S0,
  output S1,
  output S2,
  output S3,
  output C4
);

  wire and_1_out, and_2_out, and_3_out, and_4_out, and_5_out, and_6_out, and_7_out, and_8_out, or_1_out,
       or_2_out, or_3_out, xor_1_out, xor_2_out, xor_3_out, xor_4_out;

  xor xor_1 (xor_1_out, A0, B0);
  and and_1 (and_1_out, A0, B0);
  xor xor_2 (xor_2_out, A1, B1);
  and and_2 (and_2_out, A1, B1);
  xor xor_3 (xor_3_out, A2, B2);
  and and_3 (and_3_out, A2, B2);
  xor xor_4 (xor_4_out, A3, B3);
  and and_4 (and_4_out, A3, B3);
  xor xor_5 (S0, xor_1_out, C0);
  and and_5 (and_5_out, xor_1_out, C0);
  xor xor_6 (S1, xor_2_out, or_1_out);
  and and_6 (and_6_out, xor_2_out, or_1_out);
  xor xor_7 (S2, xor_3_out, or_2_out);
  and and_7 (and_7_out, xor_3_out, or_2_out);
  xor xor_8 (S3, xor_4_out, or_3_out);
  and and_8 (and_8_out, xor_4_out, or_3_out);
  or or_1 (or_1_out, and_5_out, and_1_out);
  or or_2 (or_2_out, and_6_out, and_2_out);
  or or_3 (or_3_out, and_7_out, and_3_out);
  or or_4 (C4, and_8_out, and_4_out);

  // Notes on the sheet:
  //   Sumador de 4 bits
endmodule
