// Logisim project Practica5.circ as structural Verilog: 7 circuits, main circuit AddGen
module AddGen (
  input  reset_star,
  input  clk,
  input  en,
  output q2,
  output q1,
  output q0,
  output fin
);

  wire and_1_out, and_2_out, and_3_out, not_1_out, not_2_out, not_3_out, not_4_out, or_1_out, or_2_out,
       or_3_out, or_4_out;

  not not_1 (not_1_out, en);
  not not_2 (not_2_out, q2);
  not not_3 (not_3_out, q1);
  not not_4 (not_4_out, q0);
  or or_1 (or_1_out, en, q2);
  or or_2 (or_2_out, q2, q1);
  or or_3 (or_3_out, q2, q0);
  and and_1 (and_1_out, en, q0);
  and and_2 (and_2_out, en, q0);
  and and_3 (and_3_out, or_1_out, or_2_out, or_3_out, or_4_out);
  or or_4 (or_4_out, not_1_out, not_2_out, not_3_out, not_4_out);
  D_Flip_Flop d_ff_1 (.clk(clk), .D(and_3_out), .Q(q2), .reset(reset_star));  // open: Qn, preset, en
  J_K_Flip_Flop j_k_ff_1 (.J(and_1_out), .clk(clk), .K(and_2_out), .Q(q1), .reset(reset_star));  // open: Qn, preset, en
  T_Flip_Flop t_ff_1 (.clk(clk), .T(en), .Q(q0), .reset(reset_star));  // open: Qn, preset, en
  and and_4 (fin, q0, q1, q2);
endmodule

module ALU (
  input  t1,
  input  t0,
  input  [15:0] A,
  input  [15:0] B,
  output [15:0] S,
  output Z,
  output N,
  output C,
  output V
);

  wire and_1_out, and_2_out, B_prime_15, nor_1_out, not_1_out, not_2_out, not_3_out;
  wire [15:0] A_B, B_1, B_2;

  MUX_4_1X16 mux_4_1x16_1 (.x(A_B), .y(B_1), .w(B), .g(A_B), .in_1(t1), .in_2(t0), .z({N, S[14:0]}));
  xor xor_1 (B_1[0], A[0], B[0]);
  xor xor_2 (B_1[1], A[1], B[1]);
  xor xor_3 (B_1[2], A[2], B[2]);
  xor xor_4 (B_1[3], A[3], B[3]);
  xor xor_5 (B_1[4], A[4], B[4]);
  xor xor_6 (B_1[5], A[5], B[5]);
  xor xor_7 (B_1[6], A[6], B[6]);
  xor xor_8 (B_1[7], A[7], B[7]);
  xor xor_9 (B_1[8], A[8], B[8]);
  xor xor_10 (B_1[9], A[9], B[9]);
  xor xor_11 (B_1[10], A[10], B[10]);
  xor xor_12 (B_1[11], A[11], B[11]);
  xor xor_13 (B_1[12], A[12], B[12]);
  xor xor_14 (B_1[13], A[13], B[13]);
  xor xor_15 (B_1[14], A[14], B[14]);
  xor xor_16 (B_1[15], A[15], B[15]);
  xor xor_17 (B_2[0], t0, B[0]);
  xor xor_18 (B_2[1], t0, B[1]);
  xor xor_19 (B_2[2], t0, B[2]);
  xor xor_20 (B_2[3], t0, B[3]);
  xor xor_21 (B_2[4], t0, B[4]);
  xor xor_22 (B_2[5], t0, B[5]);
  xor xor_23 (B_2[6], t0, B[6]);
  xor xor_24 (B_2[7], t0, B[7]);
  xor xor_25 (B_2[8], t0, B[8]);
  xor xor_26 (B_2[9], t0, B[9]);
  xor xor_27 (B_2[10], t0, B[10]);
  xor xor_28 (B_2[11], t0, B[11]);
  xor xor_29 (B_2[12], t0, B[12]);
  xor xor_30 (B_2[13], t0, B[13]);
  xor xor_31 (B_2[14], t0, B[14]);
  xor xor_32 (B_2[15], t0, B[15]);
  Adder #(.width(16)) adder_1 (.a(A), .b(B_2), .out(A_B), .cin(t0), .cout(C));
  not not_1 (not_1_out, A[15]);
  not not_2 (not_2_out, B_prime_15);
  not not_3 (not_3_out, N);
  and and_1 (and_1_out, not_1_out, not_2_out, N);
  and and_2 (and_2_out, A[15], B_prime_15, not_3_out);
  nor nor_1 (nor_1_out, t1, t0);
  or or_1 (V, and_1_out, and_2_out);
  nor nor_2 (Z, S[0], S[1], S[2], S[3], S[4], S[5], S[6], S[7], S[8], S[9], S[10], S[11], S[12], S[13], S[14], N);
  nand nand_1 (B_prime_15, nor_1_out, B[15]);

  assign S[15] = N;

  // Other names for the same wires on the sheet: c16 = C; S15 = N

  // Notes on the sheet:
  //   dmax B --> z=XOR+SUMADOR+MUX+NOR
  //   dmax B --> z=30+(30+20+20+(20+20)*14+30)+40+55=  785 ps
  //   Es decir: 1.27 Goperaciones/segundo
  //   Por lo tanto, F = 1/s = 1/(785*10^ -12) = 1273885350 operaciones/segundo
  //   480ps
endmodule

module MUX4_1 (
  input  x0,
  input  x1,
  input  x2,
  input  x3,
  input  s1,
  input  s0,
  output z
);

  wire and_1_out, and_2_out, and_3_out, and_4_out, not_1_out, not_2_out, not_3_out;

  not not_1 (not_1_out, s1);
  not not_2 (not_2_out, s0);
  not not_3 (not_3_out, s0);
  and and_1 (and_1_out, x0, not_1_out, not_2_out);
  and and_2 (and_2_out, x1, not_1_out, s0);
  and and_3 (and_3_out, x2, s1, not_3_out);
  and and_4 (and_4_out, x3, s1, s0);
  or or_1 (z, and_1_out, and_2_out, and_3_out, and_4_out);

  // Notes on the sheet:
  //   dx0 --> z=20+20=40ps
  //   dx1 --> z=20+20=40ps
  //   dx2 --> z=20+20=40ps
  //   dx3 --> z=20+20=40ps
  //   ds1 --> z=5+20+20=45ps
  //   ds0 --> z=5+20+20=45ps
endmodule

module MUX_4_1X16 (
  input  in_1,
  input  in_2,
  input  [15:0] x,
  input  [15:0] y,
  input  [15:0] w,
  input  [15:0] g,
  output [15:0] z
);

  MUX4_1 mux4_1_1 (.x0(x[0]), .x1(y[0]), .x2(w[0]), .x3(g[0]), .s1(in_1), .s0(in_2), .z(z[0]));
  MUX4_1 mux4_1_2 (.x0(x[1]), .x1(y[1]), .x2(w[1]), .x3(g[1]), .s1(in_1), .s0(in_2), .z(z[1]));
  MUX4_1 mux4_1_3 (.x0(x[2]), .x1(y[2]), .x2(w[2]), .x3(g[2]), .s1(in_1), .s0(in_2), .z(z[2]));
  MUX4_1 mux4_1_4 (.x0(x[3]), .x1(y[3]), .x2(w[3]), .x3(g[3]), .s1(in_1), .s0(in_2), .z(z[3]));
  MUX4_1 mux4_1_5 (.x0(x[4]), .x1(y[4]), .x2(w[4]), .x3(g[4]), .s1(in_1), .s0(in_2), .z(z[4]));
  MUX4_1 mux4_1_6 (.x0(x[5]), .x1(y[5]), .x2(w[5]), .x3(g[5]), .s1(in_1), .s0(in_2), .z(z[5]));
  MUX4_1 mux4_1_7 (.x0(x[12]), .x1(y[6]), .x2(w[6]), .x3(g[6]), .s1(in_1), .s0(in_2), .z(z[6]));
  MUX4_1 mux4_1_8 (.x0(x[7]), .x1(y[7]), .x2(w[7]), .x3(g[7]), .s1(in_1), .s0(in_2), .z(z[7]));
  MUX4_1 mux4_1_9 (.x0(x[8]), .x1(y[8]), .x2(w[8]), .x3(g[8]), .s1(in_1), .s0(in_2), .z(z[8]));
  MUX4_1 mux4_1_10 (.x0(x[9]), .x1(y[9]), .x2(w[9]), .x3(g[9]), .s1(in_1), .s0(in_2), .z(z[9]));
  MUX4_1 mux4_1_11 (.x0(x[10]), .x1(y[10]), .x2(w[10]), .x3(g[10]), .s1(in_1), .s0(in_2), .z(z[10]));
  MUX4_1 mux4_1_12 (.x0(x[11]), .x1(y[11]), .x2(w[11]), .x3(g[11]), .s1(in_1), .s0(in_2), .z(z[11]));
  MUX4_1 mux4_1_13 (.x0(x[12]), .x1(y[12]), .x2(w[12]), .x3(g[12]), .s1(in_1), .s0(in_2), .z(z[12]));
  MUX4_1 mux4_1_14 (.x0(x[13]), .x1(y[13]), .x2(w[13]), .x3(g[13]), .s1(in_1), .s0(in_2), .z(z[13]));
  MUX4_1 mux4_1_15 (.x0(x[14]), .x1(y[14]), .x2(w[14]), .x3(g[14]), .s1(in_1), .s0(in_2), .z(z[14]));
  MUX4_1 mux4_1_16 (.x0(x[15]), .x1(y[15]), .x2(w[15]), .x3(g[15]), .s1(in_1), .s0(in_2), .z(z[15]));

  assign x[6] = x[12];

  // Other names for the same wires on the sheet: s0 = in_2; s1 = in_1; x6 = x[12]
endmodule

module FD (
  input  [1:0] FLAG,
  input  [3:0] NZVC,
  output STOP
);

  wire and_1_out, and_2_out, and_3_out, and_4_out, not_1_out, not_2_out, not_3_out, not_4_out;

  not not_1 (not_1_out, FLAG[1]);
  not not_2 (not_2_out, FLAG[0]);
  not not_3 (not_3_out, FLAG[1]);
  not not_4 (not_4_out, FLAG[0]);
  and and_1 (and_1_out, not_1_out, not_2_out, NZVC[3]);
  and and_2 (and_2_out, not_3_out, FLAG[0], NZVC[2]);
  and and_3 (and_3_out, FLAG[1], not_4_out, NZVC[1]);
  and and_4 (and_4_out, FLAG[1], FLAG[0], NZVC[0]);
  or or_1 (STOP, and_1_out, and_2_out, and_3_out, and_4_out);
endmodule

module U_C (
  input  reset,
  input  clk,
  input  stop,
  input  \end ,
  output acc_en,
  output mdr_en,
  output ag_en
);

  wire q0, q1;
  wire [1:0] rom_1_data;

  ROM #(.addrWidth(4), .dataWidth(2)) rom_1 (.addr({\end , stop, q1, q0}), .data(rom_1_data));  // open: sel
  D_Flip_Flop d_ff_1 (.clk(clk), .D(rom_1_data[0]), .Q(q1), .reset(reset));  // open: Qn, preset, en
  D_Flip_Flop d_ff_2 (.clk(clk), .D(rom_1_data[1]), .Q(q0), .reset(reset));  // open: Qn, preset, en
  ROM #(.addrWidth(2), .dataWidth(3)) rom_2 (.addr(rom_1_data), .data({ag_en, mdr_en, acc_en}));  // open: sel

  // Notes on the sheet:
  //   contents of rom_1 (hex, n*v repeats v):
  //   0 2 6*3 1 2 6*3
  //   contents of rom_2 (hex, n*v repeats v):
  //   7 3 1
endmodule

module Acumulador (
  input  [1:0] flag,
  input  reset_star
);

  wire acc_en, ag_en, CLK, END, fd_1_stop, mdr_en;
  wire [2:0] addgen_1_q2;
  wire [3:0] NZVC;
  wire [15:0] MDR_q, minus_ACC, minus_ALU, rom_1_data;

  Clock u_clk (.out(CLK));
  AddGen addgen_1 (
    .reset_star(reset_star), .clk(CLK), .en(ag_en), .q2(addgen_1_q2[0]), .q1(addgen_1_q2[1]),
    .q0(addgen_1_q2[2]), .fin(END));
  FD fd_1 (.FLAG(flag), .NZVC(NZVC), .STOP(fd_1_stop));
  U_C u_c_1 (
    .reset(reset_star), .clk(CLK), .stop(fd_1_stop), .\end (END), .acc_en(acc_en), .mdr_en(mdr_en),
    .ag_en(ag_en));
  ROM #(.addrWidth(3), .dataWidth(16)) rom_1 (.addr(addgen_1_q2), .data(rom_1_data));  // open: sel
  Register #(.width(16)) MDR (.D(rom_1_data), .en(mdr_en), .Q(MDR_q), .clk(CLK), .clr(reset_star));
  // Probe on minus_ALU
  Register #(.width(16)) ACC (.D(minus_ACC), .en(acc_en), .Q(minus_ALU), .clk(CLK), .clr(reset_star));
  ALU alu_1 (
    .t1(1'b0), .t0(1'b0), .A(minus_ALU), .B(MDR_q), .S(minus_ACC), .Z(NZVC[3]), .N(NZVC[2]), .C(NZVC[1]),
    .V(NZVC[0]));

  // Notes on the sheet:
  //   contents of rom_1 (hex, n*v repeats v):
  //   7*1 1111
endmodule
