// Logisim project Practica6.circ as structural Verilog: 2 circuits, main circuit main
module main (
);

  wire a, ALU_z, b, clk, FZ, fz_t, ir, nL_E, not_1_out, pc_t, reset;
  wire [1:0] alu, CO, mux;
  wire [3:0] estado, rom_1_data;
  wire [6:0] adder_1_out, D, F, multiplexer_1_out, PC;
  wire [15:0] A_q, ALU_s, B_q, ram_1_data;

  Register #(.width(4)) u_estado (.D(rom_1_data), .Q(estado), .clk(clk), .clr(reset));  // open: en
  Register #(.width(7)) u_PC (.D(adder_1_out), .en(pc_t), .Q(PC), .clk(clk), .clr(reset));
  Register #(.width(16)) u_IR (.D(ram_1_data), .en(ir), .Q({CO, F, D}), .clk(clk));  // open: clr
  Multiplexer #(.select(2), .width(7), .enable("false")) multiplexer_1 (
    .in0(PC), .in2(F), .in3(D), .out(multiplexer_1_out), .sel(mux));  // open: in1
  ROM #(.addrWidth(7), .dataWidth(4)) rom_1 (.addr({estado, CO, FZ}), .data(rom_1_data));  // open: sel
  ROM #(.addrWidth(4), .dataWidth(10)) rom_2 (
    .addr(estado), .data({mux, alu, nL_E, pc_t, ir, a, b, fz_t}));  // open: sel
  Adder #(.width(7)) adder_1 (.a(7'b0000001), .b(multiplexer_1_out), .out(adder_1_out));  // open: cin, cout
  Register #(.width(16)) u_A (.D(ram_1_data), .en(a), .Q(A_q), .clk(clk));  // open: clr
  Register #(.width(1)) u_FZ (.D(ALU_z), .en(fz_t), .Q(FZ), .clk(clk));  // open: clr
  ALU u_ALU (.A(A_q), .B(B_q), .T(alu), .S(ALU_s), .Z(ALU_z));
  // Probe on CO
  // Probe on PC
  Register #(.width(16)) u_B (.D(ram_1_data), .en(b), .Q(B_q), .clk(clk));  // open: clr
  Button button_1 (.out(reset));
  Clock clock_1 (.out(clk));
  // Probe on D
  // Probe on F
  RAM #(.addrWidth(7), .dataWidth(16), .bus("separate")) ram_1 (
    .addr(multiplexer_1_out), .din(ALU_s), .data(ram_1_data), .str(nL_E), .sel(1'b1), .clk(clk),
    .ld(not_1_out));  // open: clr
  not not_1 (not_1_out, nL_E);
  // Probe on estado

  // Notes on the sheet:
  //   Unidad de Control (cableada 12 estados)
  //   Unidad de Proceso (ruta de datos)
  //   contents of rom_1 (hex, n*v repeats v):
  //   8*1 2 2 3 3 4 4 5 5 8*6 8*8 8*a 0 b 0 b 0 b 0 b 8*7 8*0 8*9 16*0 8*1
  //   contents of rom_2 (hex, n*v repeats v):
  //   18 0 202 202 202 0 304 321 304 41 3a1 318
  //   Control de simulación
  //   0 ADD
  //   1 CMP
  //   2 MOV
  //   3 BEQ
endmodule

module ALU (
  input  [15:0] A,
  input  [15:0] B,
  input  [1:0] T,
  output Z,
  output [15:0] S
);

  wire [15:0] adder_1_out, xor_1_out;

  Multiplexer #(.select(2), .width(16), .enable("false")) multiplexer_1 (
    .in0(adder_1_out), .in1(xor_1_out), .in2(B), .out(S), .sel(T));  // open: in3
  Adder #(.width(16)) adder_1 (.a(A), .b(B), .out(adder_1_out));  // open: cin, cout
  assign xor_1_out = A ^ B;  // XOR_Gate xor_1, 16 bits wide
  nor nor_1 (Z, S[0], S[1], S[2], S[3], S[4], S[5], S[6], S[7], S[8], S[9], S[10], S[11], S[12], S[13], S[14], S[15]);
endmodule
